// Logisim project Project.circ as structural Verilog: 5 circuits, main circuit Summation
module Summation (
  input  [3:0] in_1,
  input  [3:0] in_2,
  input  [3:0] in_3,
  output [3:0] out_4
);

  wire adder_1_cout;
  wire [3:0] adder_1_out;

  Adder #(.width(4)) adder_1 (.a(in_3), .b(in_2), .out(adder_1_out), .cin(1'b0), .cout(adder_1_cout));
  Adder #(.width(4)) adder_2 (.a(adder_1_out), .b(in_1), .out(out_4), .cin(adder_1_cout));  // open: cout
endmodule

module _7Sig_Number (
  input  A,
  input  B,
  input  C,
  output A2,
  output B2,
  output C2,
  output D,
  output E,
  output F,
  output G
);

  wire and_1_out, and_2_out, and_3_out, and_4_out, and_6_out, not_1_out, not_2_out, not_3_out, not_4_out,
       not_5_out, not_6_out, not_7_out, not_8_out, not_9_out, not_10_out, not_11_out;

  not not_1 (not_1_out, A);
  not not_2 (not_2_out, C);
  not not_3 (not_3_out, A);
  not not_4 (not_4_out, C);
  not not_5 (not_5_out, B);
  not not_6 (not_6_out, A);
  not not_7 (not_7_out, C);
  not not_8 (not_8_out, A);
  not not_9 (not_9_out, C);
  not not_10 (not_10_out, B);
  not not_11 (not_11_out, C);
  or or_1 (G, B, A);
  and and_1 (and_1_out, not_1_out, not_2_out);
  and and_2 (and_2_out, A, C);
  or or_2 (B2, not_3_out, not_4_out);
  or or_3 (C2, not_5_out, C);
  and and_3 (and_3_out, not_6_out, not_7_out);
  and and_4 (and_4_out, A, C);
  and and_5 (E, not_8_out, not_9_out);
  and and_6 (and_6_out, not_10_out, not_11_out);
  or or_4 (A2, and_1_out, B, and_2_out);
  or or_5 (D, and_3_out, B, and_4_out);
  or or_6 (F, and_6_out, A);
endmodule

module _7Sig_Result (
  input  A,
  input  B,
  input  C,
  input  D,
  input  F,
  output A2,
  output B2,
  output C2,
  output D2,
  output E,
  output F2,
  output G
);

  wire and_1_out, and_2_out, and_3_out, and_4_out, and_5_out, and_6_out, and_7_out, and_8_out, and_9_out,
       and_10_out, not_1_out, not_2_out, not_3_out, not_4_out, not_5_out, not_6_out, not_7_out, not_8_out,
       not_9_out, not_10_out, not_11_out, not_12_out, not_13_out, not_14_out;

  not not_1 (not_1_out, C);
  not not_2 (not_2_out, F);
  not not_3 (not_3_out, C);
  not not_4 (not_4_out, C);
  not not_5 (not_5_out, C);
  not not_6 (not_6_out, F);
  not not_7 (not_7_out, C);
  not not_8 (not_8_out, C);
  not not_9 (not_9_out, A);
  not not_10 (not_10_out, F);
  not not_11 (not_11_out, A);
  not not_12 (not_12_out, A);
  not not_13 (not_13_out, C);
  not not_14 (not_14_out, D);
  and and_1 (and_1_out, not_1_out, not_2_out);
  and and_2 (and_2_out, not_3_out, D);
  and and_3 (and_3_out, A, not_4_out);
  and and_4 (and_4_out, not_5_out, not_6_out);
  and and_5 (and_5_out, not_7_out, D);
  and and_6 (and_6_out, A, not_8_out);
  and and_7 (and_7_out, not_9_out, not_10_out);
  and and_8 (and_8_out, not_11_out, D);
  and and_9 (and_9_out, not_12_out, C);
  and and_10 (and_10_out, not_13_out, not_14_out, F);
  or or_1 (B2, and_1_out, and_2_out, B, and_3_out);
  or or_2 (C2, and_4_out, and_5_out, B, and_6_out);
  or or_3 (D2, and_7_out, and_8_out, and_9_out, B);
  or or_4 (G, and_10_out, B, A);

  assign A2 = 1'b1;
  assign E = 1'b1;
  assign F2 = 1'b1;
endmodule

module ProjectImplement (
  input  [3:0] in_1,
  input  [3:0] in_2,
  input  [3:0] in_3
);

  wire comparing_1_out_4, comparing_1_out_5, comparing_1_out_6, comparing_1_out_7, comparing_1_out_8,
       n7sig_number_1_a2, n7sig_number_1_b2, n7sig_number_1_c2, n7sig_number_1_d, n7sig_number_1_e,
       n7sig_number_1_f, n7sig_number_1_g, n7sig_number_2_a2, n7sig_number_2_b2, n7sig_number_2_c2,
       n7sig_number_2_d, n7sig_number_2_e, n7sig_number_2_f, n7sig_number_2_g, n7sig_number_3_a2,
       n7sig_number_3_b2, n7sig_number_3_c2, n7sig_number_3_d, n7sig_number_3_e, n7sig_number_3_f,
       n7sig_number_3_g, n7sig_result_1_a2, n7sig_result_1_b2, n7sig_result_1_c2, n7sig_result_1_d2,
       n7sig_result_1_e, n7sig_result_1_f2, n7sig_result_1_g;

  _7_Segment_Display u_7_segment_display_1 (
    .g(n7sig_number_1_g), .f(n7sig_number_1_f), .a(n7sig_number_1_a2), .b(n7sig_number_1_b2),
    .e(n7sig_number_1_e), .d(n7sig_number_1_d), .c(n7sig_number_1_c2));  // open: dp
  _7Sig_Number u_7sig_number_1 (
    .A(in_1[2]), .B(in_1[1]), .C(in_1[0]), .A2(n7sig_number_1_a2), .B2(n7sig_number_1_b2),
    .C2(n7sig_number_1_c2), .D(n7sig_number_1_d), .E(n7sig_number_1_e), .F(n7sig_number_1_f),
    .G(n7sig_number_1_g));
  _7_Segment_Display u_7_segment_display_2 (
    .g(n7sig_number_2_g), .f(n7sig_number_2_f), .a(n7sig_number_2_a2), .b(n7sig_number_2_b2),
    .e(n7sig_number_2_e), .d(n7sig_number_2_d), .c(n7sig_number_2_c2));  // open: dp
  _7Sig_Number u_7sig_number_2 (
    .A(in_2[2]), .B(in_2[1]), .C(in_2[0]), .A2(n7sig_number_2_a2), .B2(n7sig_number_2_b2),
    .C2(n7sig_number_2_c2), .D(n7sig_number_2_d), .E(n7sig_number_2_e), .F(n7sig_number_2_f),
    .G(n7sig_number_2_g));
  _7_Segment_Display u_7_segment_display_3 (
    .g(n7sig_number_3_g), .f(n7sig_number_3_f), .a(n7sig_number_3_a2), .b(n7sig_number_3_b2),
    .e(n7sig_number_3_e), .d(n7sig_number_3_d), .c(n7sig_number_3_c2));  // open: dp
  _7Sig_Number u_7sig_number_3 (
    .A(in_3[2]), .B(in_3[1]), .C(in_3[0]), .A2(n7sig_number_3_a2), .B2(n7sig_number_3_b2),
    .C2(n7sig_number_3_c2), .D(n7sig_number_3_d), .E(n7sig_number_3_e), .F(n7sig_number_3_f),
    .G(n7sig_number_3_g));
  Comparing comparing_1 (
    .in_1(in_3), .in_2(in_2), .in_3(in_1), .out_4(comparing_1_out_4), .out_5(comparing_1_out_5),
    .out_6(comparing_1_out_6), .out_7(comparing_1_out_7), .out_8(comparing_1_out_8));
  _7Sig_Result u_7sig_result_1 (
    .A(comparing_1_out_4), .B(comparing_1_out_5), .C(comparing_1_out_6), .D(comparing_1_out_7),
    .F(comparing_1_out_8), .A2(n7sig_result_1_a2), .B2(n7sig_result_1_b2), .C2(n7sig_result_1_c2),
    .D2(n7sig_result_1_d2), .E(n7sig_result_1_e), .F2(n7sig_result_1_f2), .G(n7sig_result_1_g));
  _7_Segment_Display u_7_segment_display_4 (
    .g(n7sig_result_1_g), .f(n7sig_result_1_f2), .a(n7sig_result_1_a2), .b(n7sig_result_1_b2),
    .e(n7sig_result_1_e), .d(n7sig_result_1_d2), .c(n7sig_result_1_c2));  // open: dp
endmodule

module Comparing (
  input  [3:0] in_1,
  input  [3:0] in_2,
  input  [3:0] in_3,
  output out_4,
  output out_5,
  output out_6,
  output out_7,
  output out_8
);

  wire comparator_1_eq, comparator_1_gt, comparator_1_lt, comparator_2_eq, comparator_2_gt, comparator_2_lt,
       comparator_3_eq, comparator_3_gt, comparator_3_lt, comparator_4_eq, comparator_4_gt, comparator_4_lt,
       comparator_5_eq, comparator_5_gt, n7sig_number_1_a2, n7sig_number_1_b2, n7sig_number_1_c2,
       n7sig_number_1_d, n7sig_number_1_e, n7sig_number_1_f, n7sig_number_1_g, n7sig_number_2_a2,
       n7sig_number_2_b2, n7sig_number_2_c2, n7sig_number_2_d, n7sig_number_2_e, n7sig_number_2_f,
       n7sig_number_2_g, n7sig_number_3_a2, n7sig_number_3_b2, n7sig_number_3_c2, n7sig_number_3_d,
       n7sig_number_3_e, n7sig_number_3_f, n7sig_number_3_g, or_2_out, or_3_out, or_4_out, or_5_out;
  wire [3:0] summation_1_out_4;

  _7_Segment_Display u_7_segment_display_1 (
    .g(n7sig_number_1_g), .f(n7sig_number_1_f), .a(n7sig_number_1_a2), .b(n7sig_number_1_b2),
    .e(n7sig_number_1_e), .d(n7sig_number_1_d), .c(n7sig_number_1_c2));  // open: dp
  _7Sig_Number u_7sig_number_1 (
    .A(in_1[2]), .B(in_1[1]), .C(in_1[0]), .A2(n7sig_number_1_a2), .B2(n7sig_number_1_b2),
    .C2(n7sig_number_1_c2), .D(n7sig_number_1_d), .E(n7sig_number_1_e), .F(n7sig_number_1_f),
    .G(n7sig_number_1_g));
  _7_Segment_Display u_7_segment_display_2 (
    .g(n7sig_number_2_g), .f(n7sig_number_2_f), .a(n7sig_number_2_a2), .b(n7sig_number_2_b2),
    .e(n7sig_number_2_e), .d(n7sig_number_2_d), .c(n7sig_number_2_c2));  // open: dp
  _7Sig_Number u_7sig_number_2 (
    .A(in_2[2]), .B(in_2[1]), .C(in_2[0]), .A2(n7sig_number_2_a2), .B2(n7sig_number_2_b2),
    .C2(n7sig_number_2_c2), .D(n7sig_number_2_d), .E(n7sig_number_2_e), .F(n7sig_number_2_f),
    .G(n7sig_number_2_g));
  _7_Segment_Display u_7_segment_display_3 (
    .g(n7sig_number_3_g), .f(n7sig_number_3_f), .a(n7sig_number_3_a2), .b(n7sig_number_3_b2),
    .e(n7sig_number_3_e), .d(n7sig_number_3_d), .c(n7sig_number_3_c2));  // open: dp
  _7Sig_Number u_7sig_number_3 (
    .A(in_3[2]), .B(in_3[1]), .C(in_3[0]), .A2(n7sig_number_3_a2), .B2(n7sig_number_3_b2),
    .C2(n7sig_number_3_c2), .D(n7sig_number_3_d), .E(n7sig_number_3_e), .F(n7sig_number_3_f),
    .G(n7sig_number_3_g));
  Summation summation_1 (.in_1(in_1), .in_2(in_2), .in_3(in_3), .out_4(summation_1_out_4));
  Hex_Digit_Display hex_digit_display_1 (.value(summation_1_out_4));  // open: dp
  Comparator #(.width(4), .mode("unsigned")) comparator_1 (
    .a(summation_1_out_4), .b(4'b1101), .gt(comparator_1_gt), .eq(comparator_1_eq), .lt(comparator_1_lt));
  Comparator #(.width(4), .mode("unsigned")) comparator_2 (
    .a(summation_1_out_4), .b(4'b1010), .gt(comparator_2_gt), .eq(comparator_2_eq), .lt(comparator_2_lt));
  Comparator #(.width(4), .mode("unsigned")) comparator_3 (
    .a(summation_1_out_4), .b(4'b0111), .gt(comparator_3_gt), .eq(comparator_3_eq), .lt(comparator_3_lt));
  Comparator #(.width(4), .mode("unsigned")) comparator_4 (
    .a(summation_1_out_4), .b(4'b0100), .gt(comparator_4_gt), .eq(comparator_4_eq), .lt(comparator_4_lt));
  Comparator #(.width(4), .mode("unsigned")) comparator_5 (
    .a(summation_1_out_4), .b(4'b0000), .gt(comparator_5_gt), .eq(comparator_5_eq));  // open: lt
  or or_1 (out_4, comparator_1_gt, comparator_1_eq);
  or or_2 (or_2_out, comparator_2_gt, comparator_2_eq);
  or or_3 (or_3_out, comparator_3_gt, comparator_3_eq);
  or or_4 (or_4_out, comparator_4_gt, comparator_4_eq);
  or or_5 (or_5_out, comparator_5_gt, comparator_5_eq);
  and and_1 (out_5, comparator_1_lt, or_2_out);
  and and_2 (out_6, comparator_2_lt, or_3_out);
  and and_3 (out_7, comparator_3_lt, or_4_out);
  and and_4 (out_8, comparator_4_lt, or_5_out);
endmodule
